# Fritzing sketch Untitled Sketch (saved by Fritzing 0.9.3b)
circuit board: 12.7176cm x 12.3201cm
breadboards: 1

parts:
  Part1 = Barometric Pressure Sensor - BMP180 Breakout (GY-68)
  microSD1 = MicroSD Card Module
  Part2 = Arduino Mega 2560 (Rev3)
  DHT11 = DHT11 Humitidy and Temperature Sensor
  NEO-6M = u-blox NEO-6M GPS Breakout
  LED1 = smd LED [color="Green (565nm)" package="0805 [SMD]"]
  LED2 = smd LED [color="Orange (605nm)" package="0805 [SMD]"]
  R1 = Resistor [tolerance=±5% resistance=120 package=THT]
  R2 = Resistor [tolerance=±5% resistance=120 package=THT]

nets:
  VCC: Part1.VCC, Part2.3V3
  GND: Part1.GND, microSD1.GND, Part2.GND, DHT11.GND, NEO-6M.GND, R1.Pin_0, R2.Pin_0
  N1: Part1.SCL, Part2.D21/SCL, Part2.SCL
  N2: Part1.SDA, Part2.D20/SDA, Part2.SDA
  VCC_2: microSD1.VCC, Part2.5V, DHT11.VDD, NEO-6M.VCC
  N3: microSD1.MISO, Part2.D50
  N4: microSD1.MOSI, Part2.D51
  N5: microSD1.SCK, Part2.D52
  N6: microSD1.CS, Part2.D53
  N7: Part2.D11_PWM, NEO-6M.RXD
  N8: Part2.D10_PWM, NEO-6M.TXD
  N9: Part2.D9_PWM, LED1.anode
  N10: Part2.D8_PWM, LED2.anode
  N11: Part2.D5_PWM, DHT11.DATA
  N12: LED1.cathode, R2.Pin_1
  N13: LED2.cathode, R1.Pin_1

notes:
  CS ---> 53
  SCK ---> 52
  MOSI ---> 51
  MISO ---> 50
  VCC ---> 5V
  GND ---> GND
  RX ---> 11
  TX ---> 10
  VIN ---> 3.3V
  GND ---> GND
  SCL ---> SCL
  SDA ---> SDA
  5V
  3.3V
  DATA CABLE

custom parts:
  DHT11 Humitidy and Temperature Sensor: DHT11 Humidity and Temperature Sensor

// code stored in the sketch: Untitled.ino

